// Digital circuit GPR.dig as structural Verilog
module GPR (
  input  [1:0] RegisterSelection,
  input  [1:0] CTRL,
  input  CLK,
  input  [7:0] Input,
  output [7:0] Output
);

  wire and_1_out, and_2_out, and_3_out, and_4_out, decoder_1_out_0, decoder_1_out_1, decoder_1_out_2,
       decoder_1_out_3;
  wire [7:0] R_0_p4, R_1_p4, R_2_p4, R_3_p4;

  Decoder #(.Selector_Bits(2)) decoder_1 (
    .sel(RegisterSelection), .out_0(decoder_1_out_0), .out_1(decoder_1_out_1), .out_2(decoder_1_out_2),
    .out_3(decoder_1_out_3));
  and and_1 (and_1_out, CLK, decoder_1_out_0);
  and and_2 (and_2_out, CLK, decoder_1_out_1);
  and and_3 (and_3_out, CLK, decoder_1_out_2);
  and and_4 (and_4_out, CLK, decoder_1_out_3);
  // UpdatedCircuitWControls R_0: pin names not known; wires that end beside it: and_1_out, Input, CTRL, R_0_p4
  // UpdatedCircuitWControls R_1: pin names not known; wires that end beside it: and_2_out, Input, CTRL, R_1_p4
  // UpdatedCircuitWControls R_2: pin names not known; wires that end beside it: and_3_out, Input, CTRL, R_2_p4
  // UpdatedCircuitWControls R_3: pin names not known; wires that end beside it: and_4_out, Input, CTRL, R_3_p4
  Multiplexer #(.Selector_Bits(2), .Bits(8)) multiplexer_1 (
    .sel(RegisterSelection), .in_0(R_0_p4), .in_1(R_1_p4), .in_2(R_2_p4), .in_3(R_3_p4), .out(Output));

  // Notes on the sheet:
  //   CTRL: 00->Load
  //   01->Load
  //   10->Clear
  //   11->Set FF
endmodule
