// Digital circuit SRAM.dig as structural Verilog
module SRAM (
  input  [3:0] Address,
  input  [7:0] Data_Input,
  input  Chip_Select,
  input  Write_Enable,
  input  Output_Enable,
  output [7:0] Data_Output
);

  RAMSinglePortSel #(.AddrBits(4), .Bits(8)) SRAM (
    .A(Address), .CS(Chip_Select), .WE(Write_Enable), .OE(Output_Enable), .D(Data_Input));

  assign Data_Output = Data_Input;
endmodule
